# Fritzing sketch COVID-19-Soap-Dispenser (saved by Fritzing 0.9.3b)
breadboards: 1

parts:
  Parça1 = Arduino Nano (Rev3.0)
  YL-83_-_Detection_Board1 = YL-83 Rain Sensor - Detection Board
  J1 = Piezo Speaker
  J2 = Basic Servo

nets:
  GND: Parça1.GND, YL-83_-_Detection_Board1.NEG, J1.pin1, J2.gnd
  N1: Parça1.D3, J2.pulse
  N2: Parça1.D4, J1.pin2
  5V: Parça1.5V, J2.vcc
  N3: Parça1.A0, YL-83_-_Detection_Board1.POS

custom parts:
  YL-83 Rain Sensor - Detection Board: The YL-83 is a rain sensor that has more resistance when dry and less resistance when wet. The module runs at 5V.
